# Fritzing sketch photoresistor_led_schema (saved by Fritzing 0.9.3b)
circuit board: 8.72414cm x 7.72632cm
breadboards: 1

parts:
  LED1 = LED - 5mm [color="Red (633nm)" package="5 mm [THT]"]
  LED2 = LED - 5mm [color="Green (555nm)" package="5 mm [THT]"]
  LED3 = LED - 5mm [color="Yellow (595nm)" package="5 mm [THT]"]
  R8 = Resistor [tolerance=±5% resistance=220 package=THT]
  R9 = Resistor [tolerance=±5% resistance=220 package=THT]
  R10 = Resistor [tolerance=±5% resistance=220 package=THT]
  R11 = Resistor [tolerance=±5% resistance=220 package=THT]
  R12 = Photocell (LDR) [package=THT]
  Part1 = Arduino Uno (Rev3)

nets:
  N1: LED1.cathode, R10.Pin_1
  N2: LED1.anode, Part1.D4
  N3: LED2.cathode, R8.Pin_1
  N4: LED2.anode, Part1.D3_PWM
  N5: LED3.cathode, R9.Pin_1
  N6: LED3.anode, Part1.D2
  N7: R8.Pin_0, R9.Pin_0, R10.Pin_0, R11.Pin_0, Part1.GND
  N8: R11.Pin_1, R12.pin_0, Part1.A0
  N9: R12.pin_1, Part1.5V
